# Fritzing sketch ChairSensor (saved by Fritzing 0.9.3b)
breadboards: 1

parts:
  WeMos_D1_Mini1 = WeMos D1 Mini
  U1 = Battery Holders [package=lipo-1100mAh]
  Componente1 = USB LiPoly Charger
  Keyes1 = Keyes IR Infrared Sensor Switch Module

nets:
  5V: WeMos_D1_Mini1.5V, U1.+, Componente1.VBAT, Keyes1.VCC
  N1: WeMos_D1_Mini1.D5, Keyes1.out
  GND: WeMos_D1_Mini1.G, U1.-, Componente1.GND, Keyes1.GND

custom parts:
  Keyes IR Infrared Sensor Switch Module: An infrared obstacle detector
